// Digital circuit RegisterFile_ALU.dig as structural Verilog
module RegisterFile_ALU (
  input  Clk,
  input  [1:0] Read_Register1,
  input  [1:0] Read_Register2,
  input  [3:0] Write_Data,
  input  [1:0] Write_RegisterSelect,
  input  [7:0] Ctrl_Registers,
  input  [3:0] A,
  input  [3:0] B,
  input  [2:0] Ctrl_Bits,
  output [3:0] Read_Data1,
  output [3:0] Read_Data2,
  output [3:0] D
);

  Register_File register_file_1 (
    .Select_Read1(Read_Register1), .Select_Read2(Read_Register2), .Clk(Clk), .Write_Data(Write_Data),
    .Write_Register(Write_RegisterSelect), .Ctrl_Registers(Ctrl_Registers), .ReadData_1(Read_Data1),
    .ReadData_2(Read_Data2));
  // ALU alu_1: pin names not known; wires that end beside it: A, B, Ctrl_Bits, D

  // Notes on the sheet:
  //   Register File
  //   ALU
endmodule
