// Digital circuit Register_File.dig as structural Verilog
module Register_File (
  input  [1:0] Select_Read1,
  input  [1:0] Select_Read2,
  input  Clk,
  input  [3:0] Write_Data,
  input  [1:0] Write_Register,
  input  [7:0] Ctrl_Registers,
  output [3:0] ReadData_1,
  output [3:0] ReadData_2
);

  wire [3:0] demultiplexer_1_out_0, demultiplexer_1_out_1, demultiplexer_1_out_2, demultiplexer_1_out_3,
       R_0_p4, R_1_p4, R_2_p4, R_3_p4;

  Demultiplexer #(.Bits(4), .Selector_Bits(2)) demultiplexer_1 (
    .sel(Write_Register), .in(Write_Data), .out_0(demultiplexer_1_out_0), .out_1(demultiplexer_1_out_1),
    .out_2(demultiplexer_1_out_2), .out_3(demultiplexer_1_out_3));
  // _4_bit_register R_0: pin names not known; wires that end beside it: Clk, demultiplexer_1_out_0, Ctrl_Registers[1:0], R_0_p4
  // _4_bit_register R_1: pin names not known; wires that end beside it: Clk, demultiplexer_1_out_1, Ctrl_Registers[3:2], R_1_p4
  // _4_bit_register R_2: pin names not known; wires that end beside it: Clk, demultiplexer_1_out_2, Ctrl_Registers[5:4], R_2_p4
  // _4_bit_register R_3: pin names not known; wires that end beside it: Clk, demultiplexer_1_out_3, Ctrl_Registers[7:6], R_3_p4
  Multiplexer #(.Bits(4), .Selector_Bits(2)) multiplexer_1 (
    .sel(Select_Read1), .in_0(R_0_p4), .in_1(R_1_p4), .in_2(R_2_p4), .in_3(R_3_p4), .out(ReadData_1));
  Multiplexer #(.Selector_Bits(2), .Bits(4)) multiplexer_2 (
    .sel(Select_Read2), .in_0(R_0_p4), .in_1(R_1_p4), .in_2(R_2_p4), .in_3(R_3_p4), .out(ReadData_2));
endmodule
